// Logisim project Lab4.2.circ as structural Verilog: 1 circuit, main circuit main
module main (
  input  A,
  input  B,
  input  C,
  input  D,
  output out_5,
  output out_6,
  output [3:0] out_7,
  output out_8,
  output out_9
);

  wire and_1_out, and_2_out, and_3_out, and_4_out, and_5_out, and_6_out, and_7_out, and_8_out, not_1_out,
       not_2_out, not_3_out, not_4_out;

  not not_1 (not_1_out, A);
  not not_2 (not_2_out, B);
  not not_3 (not_3_out, C);
  not not_4 (not_4_out, D);
  and and_1 (and_1_out, C, B, not_1_out);
  and and_2 (and_2_out, not_3_out, not_2_out, A);
  and and_3 (and_3_out, C, not_2_out, not_1_out);
  and and_4 (and_4_out, not_3_out, B, not_1_out);
  and and_5 (and_5_out, not_3_out, not_1_out);
  and and_6 (and_6_out, not_3_out, not_2_out);
  and and_7 (and_7_out, D, not_3_out, not_2_out);
  and and_8 (and_8_out, D, not_1_out);
  or or_1 (out_5, and_1_out, and_2_out);
  or or_2 (out_6, and_3_out, and_4_out);
  or or_3 (out_7[1], and_5_out, and_6_out);
  or or_4 (out_7[0], and_7_out, and_8_out);

  assign out_7[3:2] = {out_5, out_6};
  assign out_8 = out_7[1];
  assign out_9 = out_7[0];
endmodule
