// Logisim project odnorazryad_sum_rez.circ as structural Verilog: 1 circuit, main circuit main
module main (
  input  [7:0] in_1,
  input  [7:0] in_2,
  input  x3,
  output [7:0] out_4,
  output [7:0] out_5,
  output [7:0] out_6,
  output [7:0] out_7,
  output d
);

  wire and_1_out, and_3_out, and_5_out, and_7_out, and_9_out, and_11_out, and_13_out, not_1_out, not_2_out,
       not_3_out, not_4_out, not_5_out, not_6_out, not_7_out, not_8_out, not_9_out, not_10_out, not_11_out,
       not_12_out, not_13_out, not_14_out, not_15_out, not_16_out, not_17_out, not_18_out, not_19_out,
       not_20_out, not_21_out, not_22_out, not_23_out, not_24_out, or_1_out, or_2_out, or_3_out, or_4_out,
       or_5_out, or_6_out, or_7_out, or_8_out, or_9_out, or_10_out, or_11_out, or_12_out, or_13_out,
       or_14_out, or_15_out, or_16_out, or_17_out, or_18_out, or_19_out, or_20_out, or_21_out, or_22_out,
       or_23_out, or_24_out, or_25_out, or_26_out, or_27_out, or_28_out, or_29_out, or_30_out, or_31_out,
       or_32_out, or_33_out, or_34_out, or_35_out, or_36_out, or_37_out, or_38_out, or_39_out, or_40_out,
       or_41_out, or_42_out, or_43_out, or_44_out, or_45_out, or_46_out, or_47_out, or_48_out, or_49_out,
       or_50_out, or_51_out, or_52_out, or_53_out, or_54_out, or_55_out, or_56_out;

  not not_1 (not_1_out, in_1[0]);
  not not_2 (not_2_out, in_1[1]);
  not not_3 (not_3_out, in_1[2]);
  not not_4 (not_4_out, in_1[3]);
  not not_5 (not_5_out, in_1[4]);
  not not_6 (not_6_out, in_1[5]);
  not not_7 (not_7_out, in_1[6]);
  not not_8 (not_8_out, in_1[7]);
  not not_9 (not_9_out, x3);
  not not_10 (not_10_out, in_2[0]);
  not not_11 (not_11_out, and_1_out);
  not not_12 (not_12_out, in_2[1]);
  not not_13 (not_13_out, and_3_out);
  not not_14 (not_14_out, in_2[2]);
  not not_15 (not_15_out, and_5_out);
  not not_16 (not_16_out, in_2[3]);
  not not_17 (not_17_out, and_7_out);
  not not_18 (not_18_out, in_2[4]);
  not not_19 (not_19_out, and_9_out);
  not not_20 (not_20_out, in_2[5]);
  not not_21 (not_21_out, and_11_out);
  not not_22 (not_22_out, in_2[6]);
  not not_23 (not_23_out, and_13_out);
  not not_24 (not_24_out, in_2[7]);
  or or_1 (or_1_out, in_2[0], in_1[0]);
  or or_2 (or_2_out, in_2[0], x3);
  or or_3 (or_3_out, in_1[0], x3);
  or or_4 (or_4_out, in_2[0], in_1[0], x3);
  or or_5 (or_5_out, in_2[0], not_1_out, not_9_out);
  or or_6 (or_6_out, not_9_out, in_1[0], not_10_out);
  or or_7 (or_7_out, x3, not_10_out, not_1_out);
  or or_8 (or_8_out, in_2[1], in_1[1]);
  or or_9 (or_9_out, in_2[1], and_1_out);
  or or_10 (or_10_out, in_1[1], and_1_out);
  or or_11 (or_11_out, in_2[1], in_1[1], and_1_out);
  or or_12 (or_12_out, in_2[1], not_2_out, not_11_out);
  or or_13 (or_13_out, not_11_out, in_1[1], not_12_out);
  or or_14 (or_14_out, and_1_out, not_12_out, not_2_out);
  or or_15 (or_15_out, in_2[2], in_1[2]);
  or or_16 (or_16_out, in_2[2], and_3_out);
  or or_17 (or_17_out, in_1[2], and_3_out);
  or or_18 (or_18_out, in_2[2], in_1[2], and_3_out);
  or or_19 (or_19_out, in_2[2], not_3_out, not_13_out);
  or or_20 (or_20_out, not_13_out, in_1[2], not_14_out);
  or or_21 (or_21_out, and_3_out, not_14_out, not_3_out);
  or or_22 (or_22_out, in_2[3], in_1[3]);
  or or_23 (or_23_out, in_2[3], and_5_out);
  or or_24 (or_24_out, in_1[3], and_5_out);
  or or_25 (or_25_out, in_2[3], in_1[3], and_5_out);
  or or_26 (or_26_out, in_2[3], not_4_out, not_15_out);
  or or_27 (or_27_out, not_15_out, in_1[3], not_16_out);
  or or_28 (or_28_out, and_5_out, not_16_out, not_4_out);
  or or_29 (or_29_out, in_2[4], in_1[4]);
  or or_30 (or_30_out, in_2[4], and_7_out);
  or or_31 (or_31_out, in_1[4], and_7_out);
  or or_32 (or_32_out, in_2[4], in_1[4], and_7_out);
  or or_33 (or_33_out, in_2[4], not_5_out, not_17_out);
  or or_34 (or_34_out, not_17_out, in_1[4], not_18_out);
  or or_35 (or_35_out, and_7_out, not_18_out, not_5_out);
  or or_36 (or_36_out, in_2[5], in_1[5]);
  or or_37 (or_37_out, in_2[5], and_9_out);
  or or_38 (or_38_out, in_1[5], and_9_out);
  or or_39 (or_39_out, in_2[5], in_1[5], and_9_out);
  or or_40 (or_40_out, in_2[5], not_6_out, not_19_out);
  or or_41 (or_41_out, not_19_out, in_1[5], not_20_out);
  or or_42 (or_42_out, and_9_out, not_20_out, not_6_out);
  or or_43 (or_43_out, in_2[6], in_1[6]);
  or or_44 (or_44_out, in_2[6], and_11_out);
  or or_45 (or_45_out, in_1[6], and_11_out);
  or or_46 (or_46_out, in_2[6], in_1[6], and_11_out);
  or or_47 (or_47_out, in_2[6], not_7_out, not_21_out);
  or or_48 (or_48_out, not_21_out, in_1[6], not_22_out);
  or or_49 (or_49_out, and_11_out, not_22_out, not_7_out);
  or or_50 (or_50_out, in_2[7], in_1[7]);
  or or_51 (or_51_out, in_2[7], and_13_out);
  or or_52 (or_52_out, in_1[7], and_13_out);
  or or_53 (or_53_out, in_2[7], in_1[7], and_13_out);
  or or_54 (or_54_out, in_2[7], not_8_out, not_23_out);
  or or_55 (or_55_out, not_23_out, in_1[7], not_24_out);
  or or_56 (or_56_out, and_13_out, not_24_out, not_8_out);
  and and_1 (and_1_out, or_1_out, or_2_out, or_3_out);
  and and_2 (out_4[0], or_4_out, or_5_out, or_6_out, or_7_out);
  and and_3 (and_3_out, or_8_out, or_9_out, or_10_out);
  and and_4 (out_4[1], or_11_out, or_12_out, or_13_out, or_14_out);
  and and_5 (and_5_out, or_15_out, or_16_out, or_17_out);
  and and_6 (out_4[2], or_18_out, or_19_out, or_20_out, or_21_out);
  and and_7 (and_7_out, or_22_out, or_23_out, or_24_out);
  and and_8 (out_4[3], or_25_out, or_26_out, or_27_out, or_28_out);
  and and_9 (and_9_out, or_29_out, or_30_out, or_31_out);
  and and_10 (out_4[4], or_32_out, or_33_out, or_34_out, or_35_out);
  and and_11 (and_11_out, or_36_out, or_37_out, or_38_out);
  and and_12 (out_4[5], or_39_out, or_40_out, or_41_out, or_42_out);
  and and_13 (and_13_out, or_43_out, or_44_out, or_45_out);
  and and_14 (out_4[6], or_46_out, or_47_out, or_48_out, or_49_out);
  // AND_Gate and_15 has open pins: in0=or_50_out, in1=or_52_out, out=open
  and and_16 (out_4[7], or_53_out, or_54_out, or_55_out, or_56_out);

  assign out_5 = in_1;
  assign out_6 = out_4;
  assign out_7 = in_2;

  // Notes on the sheet:
  //   x1 x2 x3 !x1 !x2 !x3
  //   x1
  //   x2
  //   перенос
  //   сумма
  //   перенос
  //   сумма
  //   перенос
  //   сумма
  //   перенос
  //   сумма
  //   перенос
  //   сумма
  //   перенос
  //   сумма
  //   перенос
  //   сумма
  //   перенос
  //   сумма
  //   output
endmodule
