// Logisim project hggyyg.circ as structural Verilog: 1 circuit, main circuit main
module main (
  input  in_1,
  output [2:0] out_2,
  output [2:0] out_3
);

  wire and_1_out, and_2_out, clock_1_out, not_1_out, not_2_out;

  not not_1 (not_1_out, out_2[1]);
  not not_2 (not_2_out, out_2[0]);
  Clock clock_1 (.out(clock_1_out));
  and and_1 (and_1_out, not_1_out, in_1, not_2_out);
  T_Flip_Flop t_ff_1 (.T(and_1_out), .clk(clock_1_out), .Q(out_2[2]));  // open: Qn, reset, preset
  T_Flip_Flop t_ff_2 (.T(in_1), .clk(clock_1_out), .Q(out_2[0]));  // open: Qn, reset, preset
  T_Flip_Flop t_ff_3 (.T(and_2_out), .clk(clock_1_out), .Q(out_2[1]));  // open: Qn, reset, preset
  and and_2 (and_2_out, in_1, not_2_out);

  assign out_3 = out_2;
endmodule
